# Fritzing sketch Circuit Diagram (saved by Fritzing 0.9.2b)
breadboards: 1

parts:
  R1 = Resistor [tolerance=±5% resistance=330 package=THT]
  R2 = Resistor [tolerance=±5% resistance=160 package=THT]
  R3 = Resistor [tolerance=±20% resistance=160 package=THT]
  R4 = Resistor [tolerance=±5% resistance=50 package=THT]
  J1 = Piezo Speaker
  Part2 = Arduino Ethernet Shield (Rev3)
  Morse_key = Pushbutton [package=THT]
  LED1 = RGB LED (com. cathode, rgb) [package="5 mm [THT]"]

nets:
  N1: R1.Pin_0, Part2.A0
  N2: R1.Pin_1, LED1.red_anode
  N3: R2.Pin_0, Part2.A1
  N4: R2.Pin_1, LED1.green_anode
  N5: R3.Pin_0, Part2.A2
  N6: R3.Pin_1, LED1.blue_anode
  N7: R4.Pin_0, Part2.PWM_D5
  N8: R4.Pin_1, J1.pin2
  N9: J1.pin1, Part2.GND, Morse_key.leg1
  N10: Part2.A3, Morse_key.leg0
  N11: Part2.5V, LED1.common_cathode
