# Fritzing sketch TworseKey (saved by Fritzing 0.6.5b)
breadboards: 1

parts:
  Morse_Key = Pushbutton [package=THT]
  R1 = Resistor [tolerance=±5% resistance=10k package=THT]
  Buzzer = Piezo Speaker
  R2 = Resistor [tolerance=±5% resistance=50 package=THT]
  RGB_LED = RGB LED (com. anode, rbg) [package="5 mm [THT]"]
  Tworse_Key = Arduino Ethernet Shield

nets:
  N1: Morse_Key.leg0, Tworse_Key.D7
  N2: Morse_Key.leg1, Tworse_Key.GND#19
  N3: R1.Pin_0, Tworse_Key.+5V
  N4: R1.Pin_1, RGB_LED.common_anode
  N5: Buzzer.pin1, Tworse_Key.GND#20
  N6: Buzzer.pin2, R2.Pin_0
  N7: R2.Pin_1, Tworse_Key.D5
  N8: RGB_LED.red_cathode, Tworse_Key.D9
  N9: RGB_LED.green_cathode, Tworse_Key.D8
